# Fritzing sketch Color_LED (saved by Fritzing 0.7.12b)
breadboards: 1

parts:
  Arduino1 = Arduino
  LED1 = RGB LED (com. cathode, rgb) [package="5 mm [THT]"]
  R1 = Resistor [tolerance=±5% resistance=200 package=THT]
  R2 = Resistor [tolerance=±5% resistance=110 package=THT]
  R3 = Resistor [tolerance=±5% resistance=280 package=THT]

nets:
  N1: Arduino1.GND, LED1.common_cathode
  N2: Arduino1.D9, R3.Pin_1
  N3: Arduino1.D6, R2.Pin_0
  N4: Arduino1.D5, R1.Pin_0
  N5: LED1.red_anode, R1.Pin_1
  N6: LED1.green_anode, R2.Pin_1
  N7: LED1.blue_anode, R3.Pin_0
